// Logisim project 1_bit_full_adder_with_overflow.circ as structural Verilog: 1 circuit, main circuit main
module main (
  input  A,
  input  B,
  input  Cin,
  output S,
  output Cout,
  output Overflow
);

  wire and_1_out, and_2_out, and_3_out, and_4_out, and_5_out, and_6_out, and_7_out, and_8_out, and_9_out,
       not_1_out, not_2_out, not_3_out, not_4_out;

  not not_1 (not_1_out, A);
  not not_2 (not_2_out, B);
  not not_3 (not_3_out, Cin);
  and and_1 (and_1_out, not_1_out, not_2_out, Cin);
  and and_2 (and_2_out, not_1_out, B, not_3_out);
  and and_3 (and_3_out, A, not_2_out, not_3_out);
  and and_4 (and_4_out, A, B, Cin);
  and and_5 (and_5_out, B, Cin);
  and and_6 (and_6_out, A, B);
  and and_7 (and_7_out, A, Cin);
  or or_1 (S, and_1_out, and_2_out, and_3_out, and_4_out);
  or or_2 (Cout, and_5_out, and_6_out, and_7_out);
  not not_4 (not_4_out, Cout);
  and and_8 (and_8_out, Cin, not_4_out);
  and and_9 (and_9_out, not_3_out, Cout);
  or or_3 (Overflow, and_8_out, and_9_out);
endmodule
