// Logisim project 2_bits_adder.circ as structural Verilog: 1 circuit, main circuit main
module main (
  input  A1,
  input  A0,
  input  B1,
  input  B0,
  output S0,
  output S1,
  output Overflow
);

  wire main_1_cout;

  _1_bit_full_adder_main main_1 (.A(A0), .B(B0), .Cin(1'b0), .S(S0), .Cout(main_1_cout));
  _1_bit_full_adder_with_overflow_main main_2 (
    .A(A1), .B(B1), .Cin(main_1_cout), .S(S1), .Overflow(Overflow));  // open: Cout
endmodule
